// Digital circuit CPU.dig as structural Verilog
module CPU (
  input  CLK_RAW,
  input  [31:0] Breakpoint,
  output [31:0] x8_s0,
  output [31:0] x9_s1,
  output [31:0] x10_a0,
  output [31:0] PC,
  output [31:0] Address,
  output [31:0] Instr,
  output [7:0] Data_Read,
  output [5:0] Step,
  output [7:0] Substep,
  output [16:0] out_10,
  output [15:0] out_11,
  output [31:0] A,
  output [31:0] B,
  output [31:0] Result,
  output [11:0] CSR_Address,
  output [31:0] x11_a1,
  output [31:0] x4_tp,
  output [31:0] x5_t0,
  output [31:0] x6_t1,
  output [31:0] x7_t2,
  output [31:0] x1_ra,
  output [31:0] x2_sp,
  output [31:0] x3_gp,
  output [31:0] x12_a2,
  output [31:0] x13_a3,
  output [31:0] x14_a4,
  output [31:0] x15_a5,
  output [31:0] mepc,
  output [31:0] mscratch,
  output [31:0] mstatus,
  output [31:0] mie,
  output [31:0] mip,
  output [31:0] mcause,
  output [10:0] out_35,
  output [31:0] mtvec,
  output [7:0] Data_Write,
  output [31:0] Instr_2,
  output [31:0] Cycles,
  output [15:0] Instr16
);

  wire ADDR_CLK, ADDR_IN, ADDR_LATCH, ALU_A, ALU_AUX, ALU_B, ALU_N, and_1_out, and_2_out, and_4_out, B_INSTR,
       B_RUN, B_STEP, B_STOP, B_SUBSTEP, BUS_CLK, BUS_EN, BUT_INSTR, BUT_STOP, button_1_out, button_2_out,
       CLK, clock_1_lastsubstep, CNT_2, comparator_1_eq, comparator_1_gt, comparator_1_lt, comparator_2_eq,
       CS_IO, CS_RAM, CS_ROM, CSR_ADDR_LATCH, CSR_IN, CSR_IN_LATCH, CSR_OUT, CSR_OUT_LATCH, CSR_PC_OUT,
       d_ff_2_q, d_ff_3_q, d_ff_as_1_q, d_ff_as_3_q, d_ff_as_4_q, diodeforward_1_out, Imm, ImmB, ImmCSR,
       ImmI, ImmJ, ImmS, ImmU, INT1P, INT2P, INT3P, LASTSTEP, Mem_Dval, MEM_IN, MEM_OUT, MEPC_OUT,
       mie_1_mei1e, mie_1_mei2e, mie_1_mei3e, MIE_t, mip_1_mei1p, mip_1_mei2p, mip_1_mei3p, MRET, MTVEC_OUT,
       multiplexer_1_out, multiplexer_8_out, nALU_RESET, nCLK, nILL_OP, nILL_OP_FF, nIRQ, nKB_INT, nLEN4,
       nMEM_OE, nMEM_WE, nOPDONE, not_2_out, not_3_out, nREG_IN_EN, nRESET, nS_EXT, nSTEPDONE, nWAIT,
       nWAKEUP, OP_IMM_LATCH, OP_IN, OP_IN_MUX, OP_LATCH, or_1_out, PC_IN, PC_IN_LATCH, PC_IN_MUX, PC_OUT,
       PC_OUT_LATCH, REG_IN, RESET, RS1, Running, SLEEP, Stopped, switch_1_a, TRAP_OP, TRAP_OP_SnP;
  wire [0:0] LEN;
  wire [1:0] ALU_A_MUX, REG_IN_MUX, TRAP2;
  wire [2:0] ALU_OP, IMM_MUX;
  wire [3:0] RSA, RSB, RSD;
  wire [7:0] DATA;
  wire [20:18] MicroCode_d;
  wire [31:0] DATA_ADDR;

  // RGBLED rgbled_1: pin names not known; wires that end beside it: Stopped, Running, 1'b0
  Comparator #(.Bits(32)) comparator_1 (
    .a(x3_gp), .b(32'h1), .gt(comparator_1_gt), .eq(comparator_1_eq), .lt(comparator_1_lt));
  and and_1 (and_1_out, nIRQ, nILL_OP_FF);
  D_FF #(.Default(1)) d_ff_1 (.D(nILL_OP), .C(CLK), .Q(nILL_OP_FF));  // open: nQ
  // RGBLED rgbled_2: pin names not known; wires that end beside it: comparator_1_gt, comparator_1_eq, comparator_1_lt
  Comparator #(.Bits(32)) comparator_2 (.a(Breakpoint), .b(PC), .eq(comparator_2_eq));  // open: gt, lt
  Button #(.activeLow("true")) Stop (.out(BUT_STOP));
  Button #(.activeLow("true")) Run (.out(B_RUN));
  Interrupt_Controller interrupt_controller_1 (
    .BUS_CLK(BUS_CLK), .IRQ_OP_SnP(TRAP_OP_SnP), .LASTSTEP(LASTSTEP), .nIRQ(and_1_out), .OP_LATCH(OP_LATCH),
    .nRESET(nRESET), .IRQ_OP(TRAP_OP), .IRQ_OP_FETCH(OP_IN_MUX));
  and and_2 (and_2_out, nRESET, nOPDONE);
  Switch switch_1 (.A(switch_1_a), .B(comparator_1_lt));
  D_FF d_ff_2 (.D(comparator_2_eq), .C(nOPDONE), .Q(d_ff_2_q));  // open: nQ
  PullUp pullup_1 (.out(switch_1_a));
  D_FF_AS #(.Default(1)) d_ff_as_1 (.Set(nCLK), .D(1'b0), .C(d_ff_2_q), .Clr(1'b0), .Q(d_ff_as_1_q));  // open: nQ
  D_FF_AS d_ff_as_2 (.Set(~1'b1), .D(1'b1), .C(ADDR_LATCH), .Clr(~and_2_out), .Q(TRAP_OP_SnP));  // open: nQ
  Button #(.activeLow("true")) One_Instruction (.out(BUT_INSTR));
  Button #(.activeLow("true")) One_Step (.out(B_STEP));
  Button #(.activeLow("true")) One_Substep (.out(B_SUBSTEP));
  D_FF #(.Default(1)) d_ff_3 (.D(switch_1_a), .C(~nOPDONE), .Q(d_ff_3_q));  // open: nQ
  DiodeBackward diodebackward_1 (.in(d_ff_3_q), .out(B_STOP));
  DiodeBackward diodebackward_2 (.in(BUT_STOP), .out(B_STOP));
  DiodeBackward diodebackward_3 (.in(d_ff_as_1_q), .out(B_INSTR));
  DiodeBackward diodebackward_4 (.in(BUT_INSTR), .out(B_INSTR));
  PullUp pullup_2 (.out(B_STOP));
  PullUp pullup_3 (.out(B_INSTR));
  Reset reset_1 (.out(nRESET));
  Reset #(.invertOutput("false")) reset_2 (.out(RESET));
  Multiplexer multiplexer_1 (.sel(ALU_A_MUX[0]), .in_0(RS1), .in_1(PC_OUT), .out(multiplexer_1_out));
  DebugShift32 debugshift32_1 (.CLK(BUS_CLK), .D(ALU_A), .nEN(1'b0), .Val(A));
  DebugShift32 debugshift32_2 (.CLK(BUS_CLK), .D(ALU_B), .nEN(1'b0), .Val(B));
  D_FF #(.Bits(8)) d_ff_4 (.D(DATA), .C(nMEM_OE), .Q(Data_Read));  // open: nQ
  D_FF #(.Bits(8)) d_ff_5 (.D(DATA), .C(nMEM_WE), .Q(Data_Write));  // open: nQ
  PullUp pullup_4 (.out(nWAIT));
  Multiplexer multiplexer_2 (.sel(ALU_A_MUX[1]), .in_0(multiplexer_1_out), .in_1(ALU_A_MUX[0]), .out(ALU_A));
  // Mem mem_1: pin names not known; wires that end beside it: CLK, BUS_CLK, MEM_IN, ADDR_IN, ADDR_LATCH, ADDR_CLK, nMEM_OE, nMEM_WE, nS_EXT, nRESET, MEM_OUT, DATA, DATA_ADDR, Address, Mem_Dval
  Clock_driver clock_driver_1 (
    .CLK_RAW(CLK_RAW), .Stop(B_STOP), .Run(B_RUN), .One_Instruction(B_INSTR), .One_Step(B_STEP),
    .One_Substep(B_SUBSTEP), .nSTEPDONE(nSTEPDONE), .nOPDONE(OP_LATCH), .nRESET(nRESET), .nWAKEUP(nWAKEUP),
    .SLEEP(SLEEP), .nWAIT(nWAIT), .CLK(CLK), .nCLK(nCLK), .LED_R(Running), .LED_G(Running));
  nand nand_1 (nLEN4, LEN[0], BUS_EN);
  or or_1 (or_1_out, IMM_MUX[0], IMM_MUX[1], IMM_MUX[2]);
  DebugShift32 debugshift32_3 (.CLK(BUS_CLK), .D(ADDR_IN), .nEN(1'b0), .Val(Result));
  Multiplexer multiplexer_3 (.sel(or_1_out), .in_0(MEM_IN), .in_1(Imm), .out(ALU_B));
  not not_1 (Stopped, Running);
  Demultiplexer #(.Selector_Bits(2), .Default(1)) demultiplexer_1 (
    .sel(DATA_ADDR[31:30]), .in(1'b0), .out_0(CS_ROM), .out_2(CS_RAM), .out_3(CS_IO));  // open: out_1
  nor nor_1 (LASTSTEP, LEN[0], BUS_EN);
  Clock clock_1 (
    .CLK(CLK), .nCLK(nCLK), .nLEN4(nLEN4), .LASTSTEP(LASTSTEP), .SUBSTEP_EN(1'b1), .nRESET(nRESET),
    .STEP(out_10[5:0]), .LASTSUBSTEP(clock_1_lastsubstep), .nSTEPDONE(nSTEPDONE), .SUBSTEP(Substep),
    .nOPDONE(nOPDONE));
  ALU alu_1 (
    .BUS_CLK(BUS_CLK), .A(ALU_A), .B(ALU_B), .N(ALU_N), .ALU_nRESET(nALU_RESET), .ALU_AUX(ALU_AUX),
    .S(ALU_OP), .FLAG(out_10[16]), .OUT(ADDR_IN));  // open: DLEN, DSUM, C
  Terminal terminal_1 (.A(DATA_ADDR[15:0]), .nCS(CS_IO), .nWE(nMEM_WE), .nOE(nMEM_OE), .D(DATA), .nINT(nKB_INT));
  EEPROM #(.AddrBits(16), .Bits(8)) Firmware (
    .A(DATA_ADDR[15:0]), .CS(~CS_ROM), .WE(~nMEM_WE), .OE(~nMEM_OE), .D(DATA));
  RAMSinglePortSel #(.AddrBits(16), .Bits(8)) RAM (
    .A(DATA_ADDR[15:0]), .CS(~CS_RAM), .WE(~nMEM_WE), .OE(~nMEM_OE), .D(DATA));
  and and_3 (BUS_CLK, CLK, BUS_EN);
  Multiplexer multiplexer_4 (.sel(PC_IN_MUX), .in_0(ADDR_IN), .in_1(CSR_PC_OUT), .out(PC_IN));
  Multiplexer multiplexer_5 (.sel(OP_IN_MUX), .in_0(MEM_OUT), .in_1(TRAP_OP), .out(OP_IN));
  D_FF d_ff_6 (.D(OP_LATCH), .C(CLK), .Q(OP_IMM_LATCH));  // open: nQ
  Multiplexer #(.Selector_Bits(3)) multiplexer_6 (
    .sel(IMM_MUX), .in_0(ImmCSR), .in_1(ImmI), .in_2(ImmS), .in_3(ImmB), .in_4(ImmU), .in_5(ImmJ),
    .in_6(1'b0), .in_7(1'b1), .out(Imm));
  ROM #(.AddrBits(17), .isProgramMemory("true"), .Bits(32)) MicroCode (
    .A(out_10), .sel(1'b1),
    .D({REG_IN_MUX, IMM_MUX, ALU_A_MUX, PC_IN_MUX, CSR_IN_LATCH, CSR_OUT_LATCH, CSR_ADDR_LATCH, MicroCode_d, nALU_RESET, ALU_AUX, ALU_OP, ALU_N, nREG_IN_EN, nMEM_WE, nMEM_OE, ADDR_CLK, ADDR_LATCH, nILL_OP, PC_OUT_LATCH, PC_IN_LATCH, OP_LATCH, SLEEP, BUS_EN, LEN[0]}));
  PC pc_1 (
    .CLK(CLK), .BUS_CLK(BUS_CLK), .IN(PC_IN), .LATCH_IN(PC_IN_LATCH), .LATCH_OUT(PC_OUT_LATCH),
    .SnP_OUT(BUS_EN), .nPE_CNT(OP_LATCH), .EN_CNT(CNT_2), .nRESET(nRESET), .OUT(PC_OUT), .PC(PC));
  OpCode opcode_1 (
    .BUS_CLK(BUS_CLK), .IN(OP_IN), .OP_LATCH(OP_LATCH), .IMM_LATCH(OP_IMM_LATCH), .IMM_SnP(BUS_EN),
    .nRESET(nRESET), .ImmI(ImmI), .ImmS(ImmS), .ImmB(ImmB), .ImmU(ImmU), .ImmJ(ImmJ), .ImmCSR(ImmCSR),
    .RSA(RSA), .RSB(RSB), .RD(RSD), .OPCODE(out_10[10:6]), .FUNC3(out_10[13:11]), .ALU_SA(out_10[15]),
    .nS_EXT(nS_EXT), .SYS(out_10[14]), .TRAP2(TRAP2), .CNT_2(CNT_2), .Instr(Instr), .DImmI(out_11),
    .Instr16(Instr16));
  // Register_bank register_bank_1: pin names not known; wires that end beside it: BUS_CLK, REG_IN, nREG_IN_EN, RSA, RSB, RSD, RESET, RS1, MEM_IN
  Register_view register_view_1 (
    .BUS_CLK(BUS_CLK), .nREG_IN_EN(nREG_IN_EN), .REG_IN(REG_IN), .RSD(RSD), .x1_ra(x1_ra), .x2_sp(x2_sp),
    .x3_gp(x3_gp), .x4_tp(x4_tp), .x5_t0(x5_t0), .x6_t1(x6_t1), .x7_t2(x7_t2), .x8_s0_fp(x8_s0),
    .x9_s1(x9_s1), .x10_a0(x10_a0), .x11_a1(x11_a1), .x12_a2(x12_a2), .x13_a3(x13_a3), .x14_a4(x14_a4),
    .x15_a5(x15_a5));
  Multiplexer #(.Selector_Bits(2)) multiplexer_7 (
    .sel(REG_IN_MUX), .in_0(ADDR_IN), .in_1(MEM_OUT), .in_2(CSR_IN), .in_3(PC_OUT), .out(REG_IN));
  Button #(.activeLow("true")) button_1 (.out(button_1_out));
  Button #(.activeLow("true")) button_2 (.out(button_2_out));
  not not_2 (not_2_out, MRET);
  Multiplexer multiplexer_8 (.sel(out_10[13]), .in_0(RS1), .in_1(Imm), .out(multiplexer_8_out));
  PullDown pulldown_1 (.out(CSR_IN));
  and and_4 (and_4_out, not_2_out, PC_IN_MUX);
  D_FF_AS #(.Default(1)) d_ff_as_3 (.Set(CLK), .D(1'b0), .C(PC_IN_MUX), .Clr(1'b0), .Q(d_ff_as_3_q));  // open: nQ
  Counter #(.Bits(32)) counter_1 (.en(1'b1), .C(CLK), .clr(1'b0), .out(Cycles));  // open: ovf
  MIE mie_1 (
    .CLK(CLK), .BUS_CLK(BUS_CLK), .CSR_IN(CSR_OUT), .CSR_IN_LATCH(CSR_IN_LATCH),
    .CSR_OUT_LATCH(CSR_OUT_LATCH), .CSR_ADDR(CSR_Address), .nRESET(nRESET), .CSR_OUT(CSR_IN), .mie(mie),
    .MEI1E(mie_1_mei1e), .MEI2E(mie_1_mei2e), .MEI3E(mie_1_mei3e));
  MIP mip_1 (
    .CLK(CLK), .BUS_CLK(BUS_CLK), .CSR_IN(CSR_OUT), .CSR_IN_LATCH(CSR_IN_LATCH),
    .CSR_OUT_LATCH(CSR_OUT_LATCH), .CSR_ADDR(CSR_Address), .nINT1(nKB_INT), .nINT2(button_1_out),
    .nINT3(button_2_out), .nRESET(nRESET), .CSR_OUT(CSR_IN), .mip(mip), .MEI1P(mip_1_mei1p),
    .MEI2P(mip_1_mei2p), .MEI3P(mip_1_mei3p));
  MEPC mepc_1 (
    .BUS_CLK(BUS_CLK), .PC_IN(PC_OUT), .IN_EN(and_4_out), .CSR_IN(CSR_OUT), .CSR_IN_LATCH(CSR_IN_LATCH),
    .CSR_ADDR(CSR_Address), .RESET(RESET), .OUT(MEPC_OUT), .CSR_OUT(CSR_IN), .mepc(mepc));
  MSTATUS mstatus_1 (
    .CLK(CLK), .BUS_CLK(BUS_CLK), .CSR_IN(CSR_OUT), .CSR_IN_LATCH(CSR_IN_LATCH),
    .CSR_OUT_LATCH(CSR_OUT_LATCH), .CSR_ADDR(CSR_Address), .IRQ(PC_IN_MUX), .MRET(MRET),
    .IRQ_LATCH(d_ff_as_3_q), .RESET(RESET), .nRESET(nRESET), .CSR_OUT(CSR_IN), .mstatus(mstatus), .MIE(MIE_t));  // open: MPIE
  CSR csr_1 (
    .CLK(BUS_CLK), .INA(multiplexer_8_out), .INB(CSR_IN), .CSR_FUNC(out_10[12:11]), .ADDR_IN(Imm),
    .ADDR_LATCH(CSR_ADDR_LATCH), .nRESET(nRESET), .NEW_VAL(CSR_OUT), .ADDR(CSR_Address));
  Counter #(.Bits(32)) counter_2 (.en(1'b1), .C(~nOPDONE), .clr(1'b0), .out(Instr_2));  // open: ovf
  D_FF_AS #(.Default(1)) d_ff_as_4 (.Set(CLK), .D(MRET), .C(PC_IN_MUX), .Clr(1'b0), .Q(d_ff_as_4_q));  // open: nQ
  and and_5 (INT1P, mie_1_mei1e, mip_1_mei1p);
  and and_6 (INT2P, mie_1_mei2e, mip_1_mei2p);
  and and_7 (INT3P, mie_1_mei3e, mip_1_mei3p);
  not not_3 (not_3_out, TRAP2[0]);
  and and_8 (MRET, not_3_out, TRAP2[1]);
  MTVEC mtvec_1 (
    .BUS_CLK(BUS_CLK), .MTVEC_SnP(PC_IN_MUX), .CSR_IN(CSR_OUT), .CSR_IN_LATCH(CSR_IN_LATCH),
    .CSR_ADDR(CSR_Address), .RESET(RESET), .MTVEC_OUT(MTVEC_OUT), .CSR_OUT(CSR_IN), .mtvec(mtvec));
  MSCRATCH mscratch_1 (
    .BUS_CLK(BUS_CLK), .CSR_IN(CSR_OUT), .CSR_IN_LATCH(CSR_IN_LATCH), .CSR_ADDR(CSR_Address), .RESET(RESET),
    .CSR_OUT(CSR_IN), .mscratch(mscratch));
  MCAUSE mcause_1 (
    .BUS_CLK(BUS_CLK), .CSR_IN_LATCH(CSR_IN_LATCH), .CSR_OUT_LATCH(CSR_OUT_LATCH), .CSR_ADDR(CSR_Address),
    .TRAP2(TRAP2), .nIRQ(nIRQ), .INT1P(INT1P), .INT2P(INT2P), .INT3P(INT3P), .IRQ_LATCH(d_ff_as_4_q),
    .nRESET(nRESET), .CSR_OUT(CSR_IN), .mcause(mcause));
  DiodeForward diodeforward_1 (.in(INT1P), .out(diodeforward_1_out));
  DiodeForward diodeforward_2 (.in(INT2P), .out(diodeforward_1_out));
  DiodeForward diodeforward_3 (.in(INT3P), .out(diodeforward_1_out));
  Multiplexer multiplexer_9 (.sel(MRET), .in_0(MTVEC_OUT), .in_1(MEPC_OUT), .out(CSR_PC_OUT));
  PullDown pulldown_2 (.out(diodeforward_1_out));
  not not_4 (nWAKEUP, diodeforward_1_out);
  nand nand_2 (nIRQ, MIE_t, diodeforward_1_out);

  assign out_35 = out_10[16:6];
  assign Step = out_10[5:0];

  // Other names for the same wires on the sheet: IMM_SnP = BUS_EN; LEN[1] = BUS_EN; PC_OUT_SnP = BUS_EN;
  //   PC_CNT_EN = OP_LATCH; ALU_OUT = ADDR_IN; CntCycles[31:0] = Cycles; CntInstr[31:0] = Instr_2;
  //   CSR_ADDR[11:0] = CSR_Address; Da[31:0] = A; DATA_ADDR_16[15:0] = DATA_ADDR[15:0]; Db[31:0] = B;
  //   Dres[31:0] = Result; FLAG = out_10[16]; FUNC3[2:0] = out_10[13:11]; Mem_Addr[31:0] = Address;
  //   Mem_Data_R[7:0] = Data_Read; Mem_Data_W[7:0] = Data_Write; OPCODE[4:0] = out_10[10:6]; RS2 = MEM_IN;
  //   SA = out_10[15]; SYS = out_10[14]; x1[31:0] = x1_ra; x2[31:0] = x2_sp; x3[31:0] = x3_gp; x4[31:0] = x4_tp;
  //   x5[31:0] = x5_t0; x6[31:0] = x6_t1; x7[31:0] = x7_t2; x8[31:0] = x8_s0; x9[31:0] = x9_s1; x10[31:0] = x10_a0;
  //   x11[31:0] = x11_a1; x12[31:0] = x12_a2; x13[31:0] = x13_a3; x14[31:0] = x14_a4; x15[31:0] = x15_a5

  // Notes on the sheet:
  //   CLK_RAW: Hz: 20000
  //   Debug
  //   Interrupts
  //   Clock
  //   ALU
  //   Memory
  //   contents of Firmware (hex, n*v repeats v):
  //   93,0,0,0,13,1,0,0,33,87,20,0,93,3,0,0,b7,4,2,0,93,84,24,0,13,4,14,0,63,4,77,0,6f,
  //   90,50,20,93,0,10,0,13,1,10,0,33,87,20,0,93,3,20,0,b7,4,2,0,93,84,34,0,13,4,14,0,63,
  //   4,77,0,6f,90,10,1e,93,0,30,0,13,1,70,0,33,87,20,0,93,3,a0,0,b7,4,2,0,93,84,44,0,13,
  //   4,14,0,63,4,77,0,6f,90,d0,1b,93,0,0,0,37,81,ff,ff,33,87,20,0,b7,83,ff,ff,b7,4,2,0,
  //   93,84,54,0,13,4,14,0,63,4,77,0,6f,90,90,19,b7,0,0,80,13,1,0,0,33,87,20,0,b7,3,0,80,
  //   b7,4,2,0,93,84,64,0,13,4,14,0,63,4,77,0,6f,90,50,17,b7,0,0,80,37,81,ff,ff,33,87,20,
  //   0,b7,83,ff,7f,b7,4,2,0,93,84,74,0,13,4,14,0,63,4,77,0,6f,90,10,15,93,0,0,0,37,81,
  //   0,0,13,1,f1,ff,33,87,20,0,b7,83,0,0,93,83,f3,ff,b7,4,2,0,93,84,84,0,13,4,14,0,63,
  //   4,77,0,6f,90,50,12,b7,0,0,80,93,80,f0,ff,13,1,0,0,33,87,20,0,b7,3,0,80,93,83,f3,ff,
  //   b7,4,2,0,93,84,94,0,13,4,14,0,63,4,77,0,6f,90,90,f,b7,0,0,80,93,80,f0,ff,37,81,0,
  //   0,13,1,f1,ff,33,87,20,0,b7,83,0,80,93,83,e3,ff,b7,4,2,0,93,84,a4,0,13,4,14,0,63,4,
  //   77,0,6f,90,90,c,b7,0,0,80,37,81,0,0,13,1,f1,ff,33,87,20,0,b7,83,0,80,93,83,f3,ff,
  //   b7,4,2,0,93,84,b4,0,13,4,14,0,63,4,77,0,6f,90,d0,9,b7,0,0,80,93,80,f0,ff,37,81,ff,
  //   ff,33,87,20,0,b7,83,ff,7f,93,83,f3,ff,b7,4,2,0,93,84,c4,0,13,4,14,0,63,4,77,0,6f,
  //   90,10,7,93,0,0,0,13,1,f0,ff,33,87,20,0,93,3,f0,ff,b7,4,2,0,93,84,d4,0,13,4,14,0,63,
  //   4,77,0,6f,90,d0,4,93,0,f0,ff,13,1,10,0,33,87,20,0,93,3,0,0,b7,4,2,0,93,84,e4,0,13,
  //   4,14,0,63,4,77,0,6f,90,90,2,93,0,f0,ff,13,1,f0,ff,33,87,20,0,93,3,e0,ff,b7,4,2,0,
  //   93,84,f4,0,13,4,14,0,63,4,77,0,6f,90,50,0,93,0,10,0,37,1,0,80,13,1,f1,ff,33,87,20,
  //   0,b7,3,0,80,b7,4,2,0,93,84,4,1,13,4,14,0,63,4,77,0,6f,90,c0,7d,93,0,d0,0,13,1,b0,
  //   0,b3,80,20,0,93,3,80,1,b7,4,2,0,93,84,14,1,13,4,14,0,63,84,70,0,6f,90,80,7b,93,0,
  //   e0,0,13,1,b0,0,33,81,20,0,93,3,90,1,b7,4,2,0,93,84,24,1,13,4,14,0,63,4,71,0,6f,90,
  //   40,79,93,0,d0,0,b3,80,10,0,93,3,a0,1,b7,4,2,0,93,84,34,1,13,4,14,0,63,84,70,0,6f,
  //   90,40,77,13,2,0,0,93,0,d0,0,13,1,b0,0,33,87,20,0,13,3,7,0,13,2,12,0,93,2,20,0,e3,
  //   14,52,fe,93,3,80,1,b7,4,2,0,93,84,44,1,13,4,14,0,63,4,73,0,6f,90,c0,73,13,2,0,0,93,
  //   0,e0,0,13,1,b0,0,33,87,20,0,13,0,0,0,13,3,7,0,13,2,12,0,93,2,20,0,e3,12,52,fe,93,
  //   3,90,1,b7,4,2,0,93,84,54,1,13,4,14,0,63,4,73,0,6f,90,0,70,13,2,0,0,93,0,f0,0,13,1,
  //   b0,0,33,87,20,0,13,0,0,0,13,0,0,0,13,3,7,0,13,2,12,0,93,2,20,0,e3,10,52,fe,93,3,a0,
  //   1,b7,4,2,0,93,84,64,1,13,4,14,0,63,4,73,0,6f,90,0,6c,13,2,0,0,93,0,d0,0,13,1,b0,0,
  //   33,87,20,0,13,2,12,0,93,2,20,0,e3,16,52,fe,93,3,80,1,b7,4,2,0,93,84,74,1,13,4,14,
  //   0,63,4,77,0,6f,90,c0,68,13,2,0,0,93,0,e0,0,13,1,b0,0,13,0,0,0,33,87,20,0,13,2,12,
  //   0,93,2,20,0,e3,14,52,fe,93,3,90,1,b7,4,2,0,93,84,84,1,13,4,14,0,63,4,77,0,6f,90,40,
  //   65,13,2,0,0,93,0,f0,0,13,1,b0,0,13,0,0,0,13,0,0,0,33,87,20,0,13,2,12,0,93,2,20,0,
  //   e3,12,52,fe,93,3,a0,1,b7,4,2,0,93,84,94,1,13,4,14,0,63,4,77,0,6f,90,80,61,13,2,0,
  //   0,93,0,d0,0,13,0,0,0,13,1,b0,0,33,87,20,0,13,2,12,0,93,2,20,0,e3,14,52,fe,93,3,80,
  //   1,b7,4,2,0,93,84,a4,1,13,4,14,0,63,4,77,0,6f,90,0,5e,13,2,0,0,93,0,e0,0,13,0,0,0,
  //   13,1,b0,0,13,0,0,0,33,87,20,0,13,2,12,0,93,2,20,0,e3,12,52,fe,93,3,90,1,b7,4,2,0,
  //   93,84,b4,1,13,4,14,0,63,4,77,0,6f,90,40,5a,13,2,0,0,93,0,f0,0,13,0,0,0,13,0,0,0,13,
  //   1,b0,0,33,87,20,0,13,2,12,0,93,2,20,0,e3,12,52,fe,93,3,a0,1,b7,4,2,0,93,84,c4,1,13,
  //   4,14,0,63,4,77,0,6f,90,80,56,13,2,0,0,13,1,b0,0,93,0,d0,0,33,87,20,0,13,2,12,0,93,
  //   2,20,0,e3,16,52,fe,93,3,80,1,b7,4,2,0,93,84,d4,1,13,4,14,0,63,4,77,0,6f,90,40,53,
  //   13,2,0,0,13,1,b0,0,93,0,e0,0,13,0,0,0,33,87,20,0,13,2,12,0,93,2,20,0,e3,14,52,fe,
  //   93,3,90,1,b7,4,2,0,93,84,e4,1,13,4,14,0,63,4,77,0,6f,90,c0,4f,13,2,0,0,13,1,b0,0,
  //   93,0,f0,0,13,0,0,0,13,0,0,0,33,87,20,0,13,2,12,0,93,2,20,0,e3,12,52,fe,93,3,a0,1,
  //   b7,4,2,0,93,84,f4,1,13,4,14,0,63,4,77,0,6f,90,0,4c,13,2,0,0,13,1,b0,0,13,0,0,0,93,
  //   0,d0,0,33,87,20,0,13,2,12,0,93,2,20,0,e3,14,52,fe,93,3,80,1,b7,4,2,0,93,84,4,2,13,
  //   4,14,0,63,4,77,0,6f,90,80,48,13,2,0,0,13,1,b0,0,13,0,0,0,93,0,e0,0,13,0,0,0,33,87,
  //   20,0,13,2,12,0,93,2,20,0,e3,12,52,fe,93,3,90,1,b7,4,2,0,93,84,14,2,13,4,14,0,63,4,
  //   77,0,6f,90,c0,44,13,2,0,0,13,1,b0,0,13,0,0,0,13,0,0,0,93,0,f0,0,33,87,20,0,13,2,12,
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  //   PC
  //   Opcode
  //   Microcode
  //   contents of MicroCode (hex, n*v repeats v):
  //   32a32e43,32a32e43,32a32e43,32a32e43,32a32e43,32a32e43,32a32e43,32a32e43,a30ec1,a30f41,
  //   a30c41,a30e43,a30f43,a30c41,a30e43,a30f43,a30c41,a30e43,a30f43,a30c41,a30e43,a30e43,
  //   a30e49,a10e41,8a30e43,8a30e43,8a30e43,8a30e43,8a30e43,8a30e43,8a30e43,8a30e43,a30ec1,
  //   a30f41,a30c41,40a30643,40a30743,40a30643,40a30643,40a30643,40a30643,40a30643,40a30643,
  //   40a30660,0,0,0,0,0,0,0,0,0,0,0,0,0,0,0,0,0,0,0,0,32a32e43,32a32e43,32a32e43,32a32e43,
  //   32a32e43,32a32e43,32a32e43,32a32e43,a30ec1,a30f41,a30c41,a30e43,a30f43,a30c41,a30e43,
  //   a30f43,a30c41,a30e43,a30f43,a30c41,a30e43,a30e43,a30e49,a30e41,a30e01,a30e00,0,0,
  //   0,0,0,0,0,0,0,0,0,0,0,0,0,0,0,0,0,0,0,0,0,0,0,0,0,0,0,0,0,0,0,0,0,0,0,0,32a32e43,
  //   32a32e43,32a32e43,32a32e43,32a32e43,32a32e43,32a32e43,32a32e43,a30ec1,a30f41,a30c41,
  //   a30e43,a30f43,a30c41,a30e43,a30f43,a30c41,a30e43,a30f43,a30c41,a30e43,a30e43,a30e49,
  //   a30e41,a30e01,a30e00,0,0,0,0,0,0,0,0,0,0,0,0,0,0,0,0,0,0,0,0,0,0,0,0,0,0,0,0,0,0,
  //   0,0,0,0,0,0,0,0,32a32e43,32a32e43,32a32e43,32a32e43,32a32e43,32a32e43,32a32e43,32a32e43,
  //   a30ec1,a30f41,a30c41,a30e43,a30f43,a30c41,a30e43,a30f43,a30c41,a30e43,a30f43,a30c41,
  //   a30e43,a30e43,a30e49,a30e41,a30e60,0,0,0,0,0,0,0,0,0,0,0,0,0,0,0,0,0,0,0,0,0,0,0,
  //   0,0,0,0,0,0,0,0,0,0,0,0,0,0,0,0,32a32e43,32a32e43,32a32e43,32a32e43,32a32e43,32a32e43,
  //   32a32e43,32a32e43,a30ec1,a30f41,a30c41,a30e43,a30f43,a30c41,a30e43,a30f43,a30c41,
  //   a30e43,a30f43,a30c41,a30e43,a30e43,a30e49,a10e41,8a30643,8a30643,8a30643,8a30643,
  //   8a30643,8a30643,8a30643,8a30643,a30e60,0,0,0,0,0,0,0,0,0,0,0,0,0,0,0,0,0,0,0,0,0,
  //   0,0,0,0,0,0,0,0,0,0,32a32e43,32a32e43,32a32e43,32a32e43,32a32e43,32a32e43,32a32e43,
  //   32a32e43,a30ec1,a30f41,a30c41,a30e43,a30f43,a30c41,a30e43,a30f43,a30c41,a30e43,a30f43,
  //   a30c41,a30e43,a30e43,a30e49,a10e41,22a30643,22a30643,22a30643,22a30643,22a30643,22a30643,
  //   22a30643,22a30643,a30e60,0,0,0,0,0,0,0,0,0,0,0,0,0,0,0,0,0,0,0,0,0,0,0,0,0,0,0,0,
  //   0,0,0,32a32e43,32a32e43,32a32e43,32a32e43,32a32e43,32a32e43,32a32e43,32a32e43,a30ec1,
  //   a30f41,a30c41,a30e43,a30f43,a30c41,a30e43,a30f43,a30c41,a30e43,a30f43,a30c41,a30e43,
  //   a30e43,a30e49,a30e41,a30e01,a30e00,0,0,0,0,0,0,0,0,0,0,0,0,0,0,0,0,0,0,0,0,0,0,0,
  //   0,0,0,0,0,0,0,0,0,0,0,0,0,0,0,32a32e43,32a32e43,32a32e43,32a32e43,32a32e43,32a32e43,
  //   32a32e43,32a32e43,a30ec1,a30f41,a30c41,a30e43,a30f43,a30c41,a30e43,a30f43,a30c41,
  //   a30e43,a30f43,a30c41,a30e43,a30e43,a30e49,a30e41,a30e01,a30e00,0,0,0,0,0,0,0,0,0,
  //   0,0,0,0,0,0,0,0,0,0,0,0,0,0,0,0,0,0,0,0,0,0,0,0,0,0,0,0,0,32a32e43,32a32e43,32a32e43,
  //   32a32e43,32a32e43,32a32e43,32a32e43,32a32e43,a30ec1,a30f41,a30c41,a30e43,a30f43,a30c41,
  //   a30e43,a30f43,a30c41,a30e43,a30f43,a30c41,a30e43,a30e43,a30e49,a10e41,10a30e43,10a30e43,
  //   10a30e43,10a30e43,10a30e43,10a30e43,10a30e43,10a30e43,a30ec3,a30f43,a30a41,a30a43,
  //   a30a43,a30a43,a30a43,a30a43,a30a43,a30e60,0,0,0,0,0,0,0,0,0,0,0,0,0,0,0,0,0,0,0,0,
  //   0,0,32a32e43,32a32e43,32a32e43,32a32e43,32a32e43,32a32e43,32a32e43,32a32e43,a30ec1,
  //   a30f41,a30c41,a30e43,a30f43,a30c41,a30e43,a30f43,a30c41,a30e43,a30f43,a30c41,a30e43,
  //   a30e43,a30e49,a30e41,a30e01,a30e00,0,0,0,0,0,0,0,0,0,0,0,0,0,0,0,0,0,0,0,0,0,0,0,
  //   0,0,0,0,0,0,0,0,0,0,0,0,0,0,0,32a32e43,32a32e43,32a32e43,32a32e43,32a32e43,32a32e43,
  //   32a32e43,32a32e43,a30ec1,a30f41,a30c41,a30e43,a30f43,a30c41,a30e43,a30f43,a30c41,
  //   a30e43,a30f43,a30c41,a30e43,a30e43,a30e49,a30e41,a30e01,a30e00,0,0,0,0,0,0,0,0,0,
  //   0,0,0,0,0,0,0,0,0,0,0,0,0,0,0,0,0,0,0,0,0,0,0,0,0,0,0,0,0,32a32e43,32a32e43,32a32e43,
  //   32a32e43,32a32e43,32a32e43,32a32e43,32a32e43,a30ec1,a30f41,a30c41,a30e43,a30f43,a30c41,
  //   a30e43,a30f43,a30c41,a30e43,a30f43,a30c41,a30e43,a30e43,a30e49,a30e41,a30e01,a30e00,
  //   0,0,0,0,0,0,0,0,0,0,0,0,0,0,0,0,0,0,0,0,0,0,0,0,0,0,0,0,0,0,0,0,0,0,0,0,0,0,32a32e43,
  //   32a32e43,32a32e43,32a32e43,32a32e43,32a32e43,32a32e43,32a32e43,a30ec1,a30f41,a30c41,
  //   a30e43,a30f43,a30c41,a30e43,a30f43,a30c41,a30e43,a30f43,a30c41,a30e43,a30e43,a30e49,
  //   a10e41,a30643,a30643,a30643,a30643,a30643,a30643,a30643,a30643,a30e60,0,0,0,0,0,0,
  //   0,0,0,0,0,0,0,0,0,0,0,0,0,0,0,0,0,0,0,0,0,0,0,0,0,32a32e43,32a32e43,32a32e43,32a32e43,
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  //   Registers
  //   CSR
endmodule
