// Digital circuit Clock.dig as structural Verilog
module Clock (
  input  nCLK,
  input  LEN8,
  input  LEN32,
  input  nOPDONE,
  input  nRESET,
  input  CLK,
  output [4:0] STEP,
  output nLASTSUB,
  output nSUBDONE
);

  wire or_1_out, undriven, undriven_2;

  or or_1 (or_1_out, nOPDONE, nLASTSUB);
  Step_Counter step_counter_1 (.CLK(nCLK), .nRESET(nRESET), .EN(undriven_2), .nOPDONE(or_1_out), .COUNT(STEP));
  Substep_Counter substep_counter_1 (
    .nCLK(nCLK), .CLK(nRESET), .nLEN4(LEN8), .EN(LEN32), .nRESET(CLK));  // open: LAST_SUBSTEP, nSTEP_DONE, DVAL, STEP_DONE
  // Probe on undriven
endmodule

/* Test case:
CLK ~CLK ~OPDONE ~RESET LEN8 LEN32  STEP ~LASTSUB ~SUBDONE

0   1    1       0      0    0      0    0        X

1   0    1       1      0    0      0    0        X
0   1    1       1      0    0      1    0        X

1   0    1       1      0    0      1    0        X
0   1    1       1      0    0      2    0        X

1   0    1       1      0    0      2    0        X
0   1    1       1      1    0      3    1        0

loop (i,6)
1   0    1       1      1    0      3    1        1
0   1    1       1      1    0      3    1        1
end loop

1   0    1       1      1    0      3    1        1
0   1    1       1      1    0      3    0        1

1   0    1       1      1    0      3    0        0
0   1    1       1      0    0      4    0        0

1   0    1       1      0    0      4    0        0
0   1    1       1      0    1      5    1        0

loop (i,30)
1   0    1       1      0    1      5    1        1
0   1    1       1      0    1      5    1        1
end loop

1   0    1       1      0    1      5    1        1
0   1    1       1      0    1      5    0        1

1   0    1       1      0    1      5    0        0
0   1    1       1      0    1      6    1        0

loop (i,30)
1   0    1       1      0    1      6    1        1
0   1    1       1      0    1      6    1        1
end loop

1   0    1       1      0    1      6    1        1
0   1    1       1      0    1      6    0        1

1   0    1       1      0    1      6    0        0
0   1    1       1      1    0      7    1        0
  
loop (i,6)
1   0    1       1      1    0      7    1        1
0   1    1       1      1    0      7    1        1
end loop

1   0    1       1      1    0      7    1        1
0   1    1       1      1    0      7    0        1

1   0    1       1      1    0      7    0        0
0   1    1       1      0    0      8    0        0

1   0    1       1      0    0      8    0        0
0   1    0       1      1    0      9    1        0

loop (i,6)
1   0    0       1      1    0      9    1        1
0   1    0       1      1    0      9    1        1
end loop

1   0    0       1      1    0      9    1        1
0   1    0       1      1    0      9    0        1

1   0    0       1      1    0      9    0        0
0   1    1       1      0    0      0    0        0
*/
