// Digital circuit Mem.dig as structural Verilog
module Mem (
  input  CLK,
  input  IN,
  input  LATCH_IN,
  input  LATCH_OUT,
  input  SnP_OUT,
  input  ADDR_IN,
  input  LATCH_ADDR,
  input  CLK_ADDR,
  input  nPE_ADDR,
  input  nRESET,
  input  nOE,
  input  nWE,
  output OUT
);

  wire [7:0] _74hc595_1_qh, mem_decode_1_out;
  wire [31:0] mem_addr_1_addr;

  Mem_addr mem_addr_1 (
    .CLK(CLK), .IN(ADDR_IN), .LATCH(LATCH_ADDR), .CLK_MEM(CLK_ADDR), .nPE(nPE_ADDR), .nRESET(nRESET),
    .ADDR(mem_addr_1_addr));
  _74HC595 _74hc595_1 (
    .SER(IN), .SRCLK(CLK), .nSRCLR(nRESET), .RCLK(LATCH_IN), .nOE(nWE), .VCC(1'b1), .GND(1'b0),
    .QH(_74hc595_1_qh[0]), .QG(_74hc595_1_qh[1]), .QF(_74hc595_1_qh[2]), .QE(_74hc595_1_qh[3]),
    .QD(_74hc595_1_qh[4]), .QC(_74hc595_1_qh[5]), .QB(_74hc595_1_qh[6]), .QA(_74hc595_1_qh[7]));  // open: QH_2
  Mem_decode mem_decode_1 (.ADDR(mem_addr_1_addr), .IN(_74hc595_1_qh), .nOE(nOE), .nWE(nWE), .OUT(mem_decode_1_out));
  _74HC597 _74hc597_1 (
    .nMR(nRESET), .SHCP(CLK), .DS(1'b0), .STCP(LATCH_OUT), .nPL(SnP_OUT), .D7(mem_decode_1_out[0]),
    .D6(mem_decode_1_out[1]), .D5(mem_decode_1_out[2]), .D4(mem_decode_1_out[3]), .D3(mem_decode_1_out[4]),
    .D2(mem_decode_1_out[5]), .D1(mem_decode_1_out[6]), .D0(mem_decode_1_out[7]), .Q7(OUT));
endmodule

/* Test case:
CLK IN         ~OE ~WE LATCH_IN LATCH_OUT S~P_OUT ADDR_IN      LATCH_ADDR CLK_ADDR ~PE_ADDR ~RESET   OUT

0   0          1   1   0        0         1       0            0          0        1        0        0

loop (rep,32)

let addr = 0x00000000 | random(256);

# Output address
loop (i,32)
0   0          1   1   0        0         0       (addr>>i&1)  0          0        0        1        X
1   0          1   1   0        0         0       (addr>>i&1)  0          0        0        1        X
end loop

# Latch address
0   0          1   1   0        0         0       0            1          0        0        1        X
1   0          1   1   0        0         0       0            1          1        0        1        X

# Enable output and latch
0   0          0   1   0        0         0       0            0          0        1        1        X
1   0          0   1   0        1         0       0            0          0        1        1        X

# Output data
loop (i,8)
0   0          1   1   0        0         1       0            0          0        1        1        (addr>>i&1)
1   0          1   1   0        0         1       0            0          0        1        1        X
end loop

let addr = 0x80000000 | random(256);
let d0 = random(256);
let d1 = random(256);
let d2 = random(256);
let d3 = random(256);

# Output address
loop (i,32)
0   0          1   1   0        0         0       (addr>>i&1)  0          0        0        1        X
1   0          1   1   0        0         0       (addr>>i&1)  0          0        0        1        X
end loop

# Latch address
0   0          1   1   0        0         0       0            1          0        0        1        X
1   0          1   1   0        0         0       0            1          1        0        1        X

# Output data
loop (i,8)
0   (d0>>i&1)  1   1   0        0         0       0            0          0        1        1        X
1   (d0>>i&1)  1   1   0        0         0       0            0          0        1        1        X
end loop

# Latch data and write
0   0          1   1   1        0         0       0            0          0        1        1        X
0   0          1   0   1        0         0       0            0          0        1        1        X

# Output data and increase address
loop (i,8)
0   (d1>>i&1)  1   1   0        0         0       0            0          1        1        1        X
1   (d1>>i&1)  1   1   0        0         0       0            0          1        1        1        X
end loop

# Latch data and write
0   0          1   1   1        0         0       0            0          0        1        1        X
0   0          1   0   1        0         0       0            0          0        1        1        X

# Output data and increase address
loop (i,8)
0   (d2>>i&1)  1   1   0        0         0       0            0          1        1        1        X
1   (d2>>i&1)  1   1   0        0         0       0            0          1        1        1        X
end loop

# Latch data and write
0   0          1   1   1        0         0       0            0          0        1        1        X
0   0          1   0   1        0         0       0            0          0        1        1        X

# Output data and increase address
loop (i,8)
0   (d3>>i&1)  1   1   0        0         0       0            0          1        1        1        X
1   (d3>>i&1)  1   1   0        0         0       0            0          1        1        1        X
end loop

# Latch data and write
0   0          1   1   1        0         0       0            0          0        1        1        X
0   0          1   0   1        0         0       0            0          0        1        1        X

# Output address
loop (i,32)
0   0          1   1   0        0         0       (addr>>i&1)  0          0        0        1        X
1   0          1   1   0        0         0       (addr>>i&1)  0          0        0        1        X
end loop
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*/
